// Logisim project Practical-1.circ as structural Verilog: 1 circuit, main circuit main
module main (
  input  in_1,
  input  in_2,
  input  in_3,
  input  in_4,
  input  in_5,
  input  in_6,
  input  in_7,
  input  in_8,
  input  in_9,
  input  in_10,
  input  in_11,
  input  in_12,
  input  in_13
);

  wire and_1_out, nand_1_out, nor_1_out, not_1_out, or_1_out, xnor_1_out, xor_1_out;

  not not_1 (not_1_out, in_9);
  and and_1 (and_1_out, in_1, in_2);
  LED led_1 (.in(and_1_out));
  LED led_2 (.in(or_1_out));
  or or_1 (or_1_out, in_5, in_6);
  LED led_3 (.in(not_1_out));
  LED led_4 (.in(nand_1_out));
  nand nand_1 (nand_1_out, in_10, in_11);
  nor nor_1 (nor_1_out, in_12, in_13);
  LED led_5 (.in(nor_1_out));
  LED led_6 (.in(xor_1_out));
  xor xor_1 (xor_1_out, in_3, in_4);
  LED led_7 (.in(xnor_1_out));
  xnor xnor_1 (xnor_1_out, in_7, in_8);
endmodule
