// Logisim project Practical-2(NOR).circ as structural Verilog: 1 circuit, main circuit main
module main (
  input  in_1,
  input  in_2,
  input  in_3,
  input  in_4,
  input  in_5,
  input  in_6,
  input  in_7
);

  wire nor_1_out, nor_2_out, nor_3_out, nor_4_out, nor_5_out, nor_6_out, nor_7_out, nor_8_out, nor_9_out,
       nor_10_out;

  nor nor_1 (nor_1_out, in_2, in_3);
  nor nor_2 (nor_2_out, in_4, in_4);
  nor nor_3 (nor_3_out, in_5, in_5);
  nor nor_4 (nor_4_out, in_6, in_7);
  nor nor_5 (nor_5_out, in_1, in_1);
  nor nor_6 (nor_6_out, in_6, nor_4_out);
  nor nor_7 (nor_7_out, nor_4_out, in_7);
  LED led_1 (.in(nor_5_out));
  nor nor_8 (nor_8_out, nor_1_out, nor_1_out);
  LED led_2 (.in(nor_8_out));
  LED led_3 (.in(nor_9_out));
  nor nor_9 (nor_9_out, nor_2_out, nor_3_out);
  nor nor_10 (nor_10_out, nor_6_out, nor_7_out);
  LED led_4 (.in(nor_10_out));
endmodule
