// Logisim project Practical-4(a).circ as structural Verilog: 1 circuit, main circuit main
module main (
  input  in_1,
  input  in_2,
  input  in_3,
  input  in_4,
  input  in_5,
  input  in_6,
  input  in_7,
  input  in_8
);

  wire xor_1_out, xor_2_out, xor_3_out, xor_4_out, xor_5_out, xor_6_out;

  LED led_1 (.in(in_5));
  xor xor_1 (xor_1_out, in_1, in_2);
  xor xor_2 (xor_2_out, in_2, in_3);
  xor xor_3 (xor_3_out, in_3, in_4);
  xor xor_4 (xor_4_out, in_5, in_6);
  LED led_2 (.in(in_1));
  LED led_3 (.in(xor_1_out));
  LED led_4 (.in(xor_2_out));
  LED led_5 (.in(xor_3_out));
  LED led_6 (.in(xor_4_out));
  LED led_7 (.in(xor_5_out));
  xor xor_5 (xor_5_out, xor_4_out, in_7);
  LED led_8 (.in(xor_6_out));
  xor xor_6 (xor_6_out, xor_5_out, in_8);
endmodule
