// Logisim project Practical-4(c).circ as structural Verilog: 1 circuit, main circuit main
module main (
  input  A,
  input  B,
  input  C,
  input  D
);

  wire and_1_out, and_2_out, and_3_out, and_4_out, and_5_out, not_1_out, not_2_out, not_3_out, not_4_out,
       or_1_out, or_2_out, xor_1_out;

  not not_1 (not_1_out, A);
  not not_2 (not_2_out, C);
  not not_3 (not_3_out, B);
  not not_4 (not_4_out, D);
  and and_1 (and_1_out, B, D);
  and and_2 (and_2_out, B, C);
  and and_3 (and_3_out, not_3_out, D);
  and and_4 (and_4_out, not_3_out, C);
  and and_5 (and_5_out, B, not_2_out, not_4_out);
  xor xor_1 (xor_1_out, C, D);
  or or_1 (or_1_out, A, and_1_out, and_2_out);
  or or_2 (or_2_out, and_3_out, and_4_out, and_5_out);
  LED led_1 (.in(or_1_out));
  LED led_2 (.in(or_2_out));
  LED led_3 (.in(xor_1_out));
  LED led_4 (.in(D));

  // Notes on the sheet:
  //   W
  //   X
  //   Y
  //   Z
endmodule
