// Logisim project Practical-5.circ as structural Verilog: 1 circuit, main circuit main
module main (
  input  [3:0] in_1,
  input  [3:0] in_2,
  output [3:0] out_3,
  output out_4
);

  wire adder_1_cout, and_1_out, and_2_out;
  wire [2:2] or_1_out;
  wire [3:0] adder_1_out;

  Adder #(.width(4)) adder_1 (.a(in_1), .b(in_2), .out(adder_1_out), .cout(adder_1_cout));  // open: cin
  and and_1 (and_1_out, adder_1_out[3], adder_1_out[2]);
  or or_1 (or_1_out[2], adder_1_cout, and_1_out, and_2_out);
  and and_2 (and_2_out, adder_1_out[3], adder_1_out[1]);
  Adder #(.width(4)) adder_2 (
    .a(adder_1_out), .b({1'b0, {2{or_1_out[2]}}, 1'b0}), .out(out_3), .cout(out_4));  // open: cin
endmodule
